// Logisim project main.circ as structural Verilog: 27 circuits, main circuit TwoBitAdder
module TwoBitAdder (
  input  [1:0] A,
  input  [1:0] B,
  input  C_in,
  output [1:0] Sum,
  output C_out
);

  wire and_1_out, and_2_out, and_3_out, and_4_out, or_1_out, xor_1_out, xor_3_out;

  xor xor_1 (xor_1_out, A[0], B[0]);
  xor xor_2 (Sum[0], xor_1_out, C_in);
  and and_1 (and_1_out, xor_1_out, C_in);
  and and_2 (and_2_out, A[0], B[0]);
  or or_1 (or_1_out, and_1_out, and_2_out);
  xor xor_3 (xor_3_out, A[1], B[1]);
  xor xor_4 (Sum[1], xor_3_out, or_1_out);
  and and_3 (and_3_out, xor_3_out, or_1_out);
  and and_4 (and_4_out, A[1], B[1]);
  or or_2 (C_out, and_3_out, and_4_out);

  // Notes on the sheet:
  //   External Carry
  //   S1
  //   Two Bit Adder
  //   B1
  //   B2
  //   S2
  //   Carry-out
endmodule

module FourBitAdder (
  input  [3:0] A,
  input  [3:0] B,
  input  C_in,
  output [3:0] Sum,
  output C_out
);

  wire twobitadder_1_c_out;

  TwoBitAdder twobitadder_1 (.A(A[1:0]), .B(B[1:0]), .C_in(C_in), .Sum(Sum[1:0]), .C_out(twobitadder_1_c_out));
  TwoBitAdder twobitadder_2 (.A(A[3:2]), .B(B[3:2]), .C_in(twobitadder_1_c_out), .Sum(Sum[3:2]), .C_out(C_out));
endmodule

module EightBitAdder (
  input  [7:0] A,
  input  [7:0] B,
  input  C_in,
  output [7:0] Sum,
  output C_out
);

  wire fourbitadder_1_c_out;

  FourBitAdder fourbitadder_1 (.A(A[3:0]), .B(B[3:0]), .C_in(C_in), .Sum(Sum[3:0]), .C_out(fourbitadder_1_c_out));
  FourBitAdder fourbitadder_2 (.A(A[7:4]), .B(B[7:4]), .C_in(fourbitadder_1_c_out), .Sum(Sum[7:4]), .C_out(C_out));
endmodule

module SixteenBitAdder (
  input  [15:0] A,
  input  [15:0] B,
  input  C_in,
  output [15:0] Sum,
  output C_out
);

  wire eightbitadder_1_c_out;

  EightBitAdder eightbitadder_1 (.A(A[7:0]), .B(B[7:0]), .C_in(C_in), .Sum(Sum[7:0]), .C_out(eightbitadder_1_c_out));
  EightBitAdder eightbitadder_2 (
    .A(A[15:8]), .B(B[15:8]), .C_in(eightbitadder_1_c_out), .Sum(Sum[15:8]), .C_out(C_out));
endmodule

module SixteenBitSubtractor (
  input  [15:0] A,
  input  [15:0] B,
  output [15:0] out_3,
  output borrow_out
);

  wire [15:0] not_1_out;

  assign not_1_out = ~B;  // NOT_Gate not_1, 16 bits wide
  SixteenBitAdder sixteenbitadder_1 (.A(A), .B(not_1_out), .C_in(1'b1), .Sum(out_3), .C_out(borrow_out));
endmodule

module SixteenBitIncrement (
  input  [15:0] A,
  output [15:0] Increment
);

  SixteenBitAdder sixteenbitadder_1 (.A(A), .B({16{1'b0}}), .C_in(1'b1), .Sum(Increment));  // open: C_out
endmodule

module SixteenBitDecrement (
  input  [15:0] A,
  output [15:0] Decrement
);

  SixteenBitSubtractor sixteenbitsubtractor_1 (.A(A), .B(16'h1), .out_3(Decrement));  // open: borrow_out
endmodule

module Enabled_D_FlipFlop (
  input  D,
  input  clk,
  input  Enable,
  output Q,
  output Q_not
);

  wire multiplexer_1_out;

  Multiplexer multiplexer_1 (.in0(Q), .in1(D), .out(multiplexer_1_out), .sel(Enable));
  D_Flip_Flop d_ff_1 (.D(multiplexer_1_out), .clk(clk), .Q(Q), .Qn(Q_not));  // open: preset, reset
endmodule

module MyRegister (
  input  [7:0] input_bits,
  input  clk,
  input  enable,
  output [7:0] output_bits
);

  Enabled_D_FlipFlop enabled_d_flipflop_1 (
    .D(input_bits[0]), .clk(clk), .Enable(enable), .Q(output_bits[0]));  // open: Q_not
  Enabled_D_FlipFlop enabled_d_flipflop_2 (
    .D(input_bits[1]), .clk(clk), .Enable(enable), .Q(output_bits[1]));  // open: Q_not
  Enabled_D_FlipFlop enabled_d_flipflop_3 (
    .D(input_bits[2]), .clk(clk), .Enable(enable), .Q(output_bits[2]));  // open: Q_not
  Enabled_D_FlipFlop enabled_d_flipflop_4 (
    .D(input_bits[3]), .clk(clk), .Enable(enable), .Q(output_bits[3]));  // open: Q_not
  Enabled_D_FlipFlop enabled_d_flipflop_5 (
    .D(input_bits[4]), .clk(clk), .Enable(enable), .Q(output_bits[4]));  // open: Q_not
  Enabled_D_FlipFlop enabled_d_flipflop_6 (
    .D(input_bits[5]), .clk(clk), .Enable(enable), .Q(output_bits[5]));  // open: Q_not
  Enabled_D_FlipFlop enabled_d_flipflop_7 (
    .D(input_bits[6]), .clk(clk), .Enable(enable), .Q(output_bits[6]));  // open: Q_not
  Enabled_D_FlipFlop enabled_d_flipflop_8 (
    .D(input_bits[7]), .clk(clk), .Enable(enable), .Q(output_bits[7]));  // open: Q_not
endmodule

module Sixteen_Bit_Register (
  input  [15:0] input_bits,
  input  clk,
  input  enable,
  output [15:0] out_4
);

  MyRegister myregister_1 (.input_bits(input_bits[7:0]), .clk(clk), .enable(enable), .output_bits(out_4[7:0]));
  MyRegister myregister_2 (.input_bits(input_bits[15:8]), .clk(clk), .enable(enable), .output_bits(out_4[15:8]));
endmodule

module Twelve_Bit_Register (
  input  [11:0] input_bits,
  input  clk,
  input  LD,
  output [11:0] output_bits
);

  Enabled_D_FlipFlop enabled_d_flipflop_1 (
    .D(input_bits[0]), .clk(clk), .Enable(LD), .Q(output_bits[0]));  // open: Q_not
  Enabled_D_FlipFlop enabled_d_flipflop_2 (
    .D(input_bits[1]), .clk(clk), .Enable(LD), .Q(output_bits[1]));  // open: Q_not
  Enabled_D_FlipFlop enabled_d_flipflop_3 (
    .D(input_bits[2]), .clk(clk), .Enable(LD), .Q(output_bits[2]));  // open: Q_not
  Enabled_D_FlipFlop enabled_d_flipflop_4 (
    .D(input_bits[3]), .clk(clk), .Enable(LD), .Q(output_bits[3]));  // open: Q_not
  Enabled_D_FlipFlop enabled_d_flipflop_5 (
    .D(input_bits[4]), .clk(clk), .Enable(LD), .Q(output_bits[4]));  // open: Q_not
  Enabled_D_FlipFlop enabled_d_flipflop_6 (
    .D(input_bits[5]), .clk(clk), .Enable(LD), .Q(output_bits[5]));  // open: Q_not
  Enabled_D_FlipFlop enabled_d_flipflop_7 (
    .D(input_bits[6]), .clk(clk), .Enable(LD), .Q(output_bits[6]));  // open: Q_not
  Enabled_D_FlipFlop enabled_d_flipflop_8 (
    .D(input_bits[7]), .clk(clk), .Enable(LD), .Q(output_bits[7]));  // open: Q_not
  Enabled_D_FlipFlop enabled_d_flipflop_9 (
    .D(input_bits[8]), .clk(clk), .Enable(LD), .Q(output_bits[8]));  // open: Q_not
  Enabled_D_FlipFlop enabled_d_flipflop_10 (
    .D(input_bits[9]), .clk(clk), .Enable(LD), .Q(output_bits[9]));  // open: Q_not
  Enabled_D_FlipFlop enabled_d_flipflop_11 (
    .D(input_bits[10]), .clk(clk), .Enable(LD), .Q(output_bits[10]));  // open: Q_not
  Enabled_D_FlipFlop enabled_d_flipflop_12 (
    .D(input_bits[11]), .clk(clk), .Enable(LD), .Q(output_bits[11]));  // open: Q_not
endmodule

module TwoxFour_Decoder (
  input  [1:0] select_bits,
  input  enable,
  output [3:0] out_3
);

  wire not_1_out, not_2_out;

  not not_1 (not_1_out, select_bits[0]);
  not not_2 (not_2_out, select_bits[1]);
  and and_1 (out_3[0], not_2_out, not_1_out, enable);
  and and_2 (out_3[1], select_bits[0], not_2_out, enable);
  and and_3 (out_3[2], select_bits[1], not_1_out, enable);
  and and_4 (out_3[3], select_bits[1], select_bits[0], enable);
endmodule

module ThreebyEight_Decoder (
  input  [2:0] select_bits,
  input  enable,
  output [7:0] output_bits
);

  wire and_1_out, and_2_out, not_1_out;

  not not_1 (not_1_out, select_bits[2]);
  and and_1 (and_1_out, not_1_out, enable);
  and and_2 (and_2_out, select_bits[2], enable);
  TwoxFour_Decoder twoxfour_decoder_1 (.select_bits(select_bits[1:0]), .enable(and_1_out), .out_3(output_bits[3:0]));
  TwoxFour_Decoder twoxfour_decoder_2 (.select_bits(select_bits[1:0]), .enable(and_2_out), .out_3(output_bits[7:4]));
endmodule

module FourbySixteen_Decoder (
  input  [3:0] in_1,
  input  enable,
  output [15:0] out_3
);

  wire and_1_out, and_2_out, not_1_out;

  not not_1 (not_1_out, in_1[3]);
  and and_1 (and_1_out, in_1[3], enable);
  and and_2 (and_2_out, not_1_out, enable);
  ThreebyEight_Decoder threebyeight_decoder_1 (.select_bits(in_1[2:0]), .enable(and_2_out), .output_bits(out_3[7:0]));
  ThreebyEight_Decoder threebyeight_decoder_2 (.select_bits(in_1[2:0]), .enable(and_1_out), .output_bits(out_3[15:8]));
endmodule

module Left_Right_Shifter (
  input  [15:0] A,
  input  [1:0] mode,
  output [15:0] out_3
);

  wire clock_1_out, multiplexer_1_out, multiplexer_2_out, multiplexer_3_out, multiplexer_4_out,
       multiplexer_5_out, multiplexer_6_out, multiplexer_7_out, multiplexer_8_out, multiplexer_9_out,
       multiplexer_10_out, multiplexer_11_out, multiplexer_12_out, multiplexer_13_out, multiplexer_14_out,
       multiplexer_15_out, multiplexer_16_out;

  Clock clock_1 (.out(clock_1_out));
  Multiplexer #(.select(2)) multiplexer_1 (
    .in0(out_3[0]), .in1(A[0]), .in2(out_3[1]), .in3(1'b0), .out(multiplexer_1_out), .sel(mode));
  Multiplexer #(.select(2)) multiplexer_2 (
    .in0(out_3[1]), .in1(A[1]), .in2(out_3[2]), .in3(out_3[0]), .out(multiplexer_2_out), .sel(mode));
  Multiplexer #(.select(2)) multiplexer_3 (
    .in0(out_3[2]), .in1(A[2]), .in2(out_3[3]), .in3(out_3[1]), .out(multiplexer_3_out), .sel(mode));
  Multiplexer #(.select(2)) multiplexer_4 (
    .in0(out_3[3]), .in1(A[3]), .in2(out_3[4]), .in3(out_3[2]), .out(multiplexer_4_out), .sel(mode));
  Multiplexer #(.select(2)) multiplexer_5 (
    .in0(out_3[4]), .in1(A[4]), .in2(out_3[5]), .in3(out_3[3]), .out(multiplexer_5_out), .sel(mode));
  Multiplexer #(.select(2)) multiplexer_6 (
    .in0(out_3[5]), .in1(A[5]), .in2(out_3[6]), .in3(out_3[4]), .out(multiplexer_6_out), .sel(mode));
  Multiplexer #(.select(2)) multiplexer_7 (
    .in0(out_3[6]), .in1(A[6]), .in2(out_3[7]), .in3(out_3[5]), .out(multiplexer_7_out), .sel(mode));
  Multiplexer #(.select(2)) multiplexer_8 (
    .in0(out_3[7]), .in1(A[7]), .in2(out_3[8]), .in3(out_3[6]), .out(multiplexer_8_out), .sel(mode));
  Multiplexer #(.select(2)) multiplexer_9 (
    .in0(out_3[8]), .in1(A[8]), .in2(out_3[9]), .in3(out_3[7]), .out(multiplexer_9_out), .sel(mode));
  Multiplexer #(.select(2)) multiplexer_10 (
    .in0(out_3[10]), .in1(A[10]), .in2(out_3[11]), .in3(out_3[9]), .out(multiplexer_10_out), .sel(mode));
  Multiplexer #(.select(2)) multiplexer_11 (
    .in0(out_3[11]), .in1(A[11]), .in2(out_3[12]), .in3(out_3[10]), .out(multiplexer_11_out), .sel(mode));
  Multiplexer #(.select(2)) multiplexer_12 (
    .in0(out_3[12]), .in1(A[12]), .in2(out_3[13]), .in3(out_3[11]), .out(multiplexer_12_out), .sel(mode));
  Multiplexer #(.select(2)) multiplexer_13 (
    .in0(out_3[13]), .in1(A[13]), .in2(out_3[14]), .in3(out_3[12]), .out(multiplexer_13_out), .sel(mode));
  Multiplexer #(.select(2)) multiplexer_14 (
    .in0(out_3[14]), .in1(A[14]), .in2(out_3[15]), .in3(out_3[13]), .out(multiplexer_14_out), .sel(mode));
  Multiplexer #(.select(2)) multiplexer_15 (
    .in0(out_3[15]), .in1(A[15]), .in2(1'b0), .in3(out_3[14]), .out(multiplexer_15_out), .sel(mode));
  Multiplexer #(.select(2)) multiplexer_16 (
    .in0(out_3[9]), .in1(A[9]), .in2(out_3[10]), .in3(out_3[8]), .out(multiplexer_16_out), .sel(mode));
  D_Flip_Flop d_ff_1 (.D(multiplexer_1_out), .clk(clock_1_out), .Q(out_3[0]));  // open: Qn, preset, reset
  D_Flip_Flop d_ff_2 (.D(multiplexer_2_out), .clk(clock_1_out), .Q(out_3[1]));  // open: Qn, preset, reset
  D_Flip_Flop d_ff_3 (.D(multiplexer_3_out), .clk(clock_1_out), .Q(out_3[2]));  // open: Qn, preset, reset
  D_Flip_Flop d_ff_4 (.D(multiplexer_4_out), .clk(clock_1_out), .Q(out_3[3]));  // open: Qn, preset, reset
  D_Flip_Flop d_ff_5 (.D(multiplexer_5_out), .clk(clock_1_out), .Q(out_3[4]));  // open: Qn, preset, reset
  D_Flip_Flop d_ff_6 (.D(multiplexer_6_out), .clk(clock_1_out), .Q(out_3[5]));  // open: Qn, preset, reset
  D_Flip_Flop d_ff_7 (.D(multiplexer_7_out), .clk(clock_1_out), .Q(out_3[6]));  // open: Qn, preset, reset
  D_Flip_Flop d_ff_8 (.D(multiplexer_8_out), .clk(clock_1_out), .Q(out_3[7]));  // open: Qn, preset, reset
  D_Flip_Flop d_ff_9 (.D(multiplexer_9_out), .clk(clock_1_out), .Q(out_3[8]));  // open: Qn, preset, reset
  D_Flip_Flop d_ff_10 (.D(multiplexer_16_out), .clk(clock_1_out), .Q(out_3[9]));  // open: Qn, preset, reset
  D_Flip_Flop d_ff_11 (.D(multiplexer_10_out), .clk(clock_1_out), .Q(out_3[10]));  // open: Qn, preset, reset
  D_Flip_Flop d_ff_12 (.D(multiplexer_11_out), .clk(clock_1_out), .Q(out_3[11]));  // open: Qn, preset, reset
  D_Flip_Flop d_ff_13 (.D(multiplexer_12_out), .clk(clock_1_out), .Q(out_3[12]));  // open: Qn, preset, reset
  D_Flip_Flop d_ff_14 (.D(multiplexer_13_out), .clk(clock_1_out), .Q(out_3[13]));  // open: Qn, preset, reset
  D_Flip_Flop d_ff_15 (.D(multiplexer_14_out), .clk(clock_1_out), .Q(out_3[14]));  // open: Qn, preset, reset
  D_Flip_Flop d_ff_16 (.D(multiplexer_15_out), .clk(clock_1_out), .Q(out_3[15]));  // open: Qn, preset, reset
endmodule

module Left_Right_Circular_Shifter (
  input  [15:0] A,
  input  [1:0] mode,
  input  clk,
  output [15:0] out_4
);

  wire multiplexer_1_out, multiplexer_2_out, multiplexer_3_out, multiplexer_4_out, multiplexer_5_out,
       multiplexer_6_out, multiplexer_7_out, multiplexer_8_out, multiplexer_9_out, multiplexer_10_out,
       multiplexer_11_out, multiplexer_12_out, multiplexer_13_out, multiplexer_14_out, multiplexer_15_out,
       multiplexer_16_out;

  Multiplexer #(.select(2)) multiplexer_1 (
    .in0(out_4[0]), .in1(A[0]), .in2(out_4[1]), .in3(out_4[15]), .out(multiplexer_1_out), .sel(mode));
  Multiplexer #(.select(2)) multiplexer_2 (
    .in0(out_4[1]), .in1(A[1]), .in2(out_4[2]), .in3(out_4[0]), .out(multiplexer_2_out), .sel(mode));
  Multiplexer #(.select(2)) multiplexer_3 (
    .in0(out_4[2]), .in1(A[2]), .in2(out_4[3]), .in3(out_4[1]), .out(multiplexer_3_out), .sel(mode));
  Multiplexer #(.select(2)) multiplexer_4 (
    .in0(out_4[3]), .in1(A[3]), .in2(out_4[4]), .in3(out_4[2]), .out(multiplexer_4_out), .sel(mode));
  Multiplexer #(.select(2)) multiplexer_5 (
    .in0(out_4[4]), .in1(A[4]), .in2(out_4[5]), .in3(out_4[3]), .out(multiplexer_5_out), .sel(mode));
  Multiplexer #(.select(2)) multiplexer_6 (
    .in0(out_4[5]), .in1(A[5]), .in2(out_4[6]), .in3(out_4[4]), .out(multiplexer_6_out), .sel(mode));
  Multiplexer #(.select(2)) multiplexer_7 (
    .in0(out_4[6]), .in1(A[6]), .in2(out_4[7]), .in3(out_4[5]), .out(multiplexer_7_out), .sel(mode));
  Multiplexer #(.select(2)) multiplexer_8 (
    .in0(out_4[7]), .in1(A[7]), .in2(out_4[8]), .in3(out_4[6]), .out(multiplexer_8_out), .sel(mode));
  Multiplexer #(.select(2)) multiplexer_9 (
    .in0(out_4[8]), .in1(A[8]), .in2(out_4[9]), .in3(out_4[7]), .out(multiplexer_9_out), .sel(mode));
  Multiplexer #(.select(2)) multiplexer_10 (
    .in0(out_4[10]), .in1(A[10]), .in2(out_4[11]), .in3(out_4[9]), .out(multiplexer_10_out), .sel(mode));
  Multiplexer #(.select(2)) multiplexer_11 (
    .in0(out_4[11]), .in1(A[11]), .in2(out_4[12]), .in3(out_4[10]), .out(multiplexer_11_out), .sel(mode));
  Multiplexer #(.select(2)) multiplexer_12 (
    .in0(out_4[12]), .in1(A[12]), .in2(out_4[13]), .in3(out_4[11]), .out(multiplexer_12_out), .sel(mode));
  Multiplexer #(.select(2)) multiplexer_13 (
    .in0(out_4[13]), .in1(A[13]), .in2(out_4[14]), .in3(out_4[12]), .out(multiplexer_13_out), .sel(mode));
  Multiplexer #(.select(2)) multiplexer_14 (
    .in0(out_4[14]), .in1(A[14]), .in2(out_4[15]), .in3(out_4[13]), .out(multiplexer_14_out), .sel(mode));
  Multiplexer #(.select(2)) multiplexer_15 (
    .in0(out_4[15]), .in1(A[15]), .in2(out_4[0]), .in3(out_4[14]), .out(multiplexer_15_out), .sel(mode));
  Multiplexer #(.select(2)) multiplexer_16 (
    .in0(out_4[9]), .in1(A[9]), .in2(out_4[10]), .in3(out_4[8]), .out(multiplexer_16_out), .sel(mode));
  D_Flip_Flop d_ff_1 (.D(multiplexer_1_out), .clk(clk), .Q(out_4[0]));  // open: Qn, preset, reset
  D_Flip_Flop d_ff_2 (.D(multiplexer_2_out), .clk(clk), .Q(out_4[1]));  // open: Qn, preset, reset
  D_Flip_Flop d_ff_3 (.D(multiplexer_3_out), .clk(clk), .Q(out_4[2]));  // open: Qn, preset, reset
  D_Flip_Flop d_ff_4 (.D(multiplexer_4_out), .clk(clk), .Q(out_4[3]));  // open: Qn, preset, reset
  D_Flip_Flop d_ff_5 (.D(multiplexer_5_out), .clk(clk), .Q(out_4[4]));  // open: Qn, preset, reset
  D_Flip_Flop d_ff_6 (.D(multiplexer_6_out), .clk(clk), .Q(out_4[5]));  // open: Qn, preset, reset
  D_Flip_Flop d_ff_7 (.D(multiplexer_7_out), .clk(clk), .Q(out_4[6]));  // open: Qn, preset, reset
  D_Flip_Flop d_ff_8 (.D(multiplexer_8_out), .clk(clk), .Q(out_4[7]));  // open: Qn, preset, reset
  D_Flip_Flop d_ff_9 (.D(multiplexer_9_out), .clk(clk), .Q(out_4[8]));  // open: Qn, preset, reset
  D_Flip_Flop d_ff_10 (.D(multiplexer_16_out), .clk(clk), .Q(out_4[9]));  // open: Qn, preset, reset
  D_Flip_Flop d_ff_11 (.D(multiplexer_10_out), .clk(clk), .Q(out_4[10]));  // open: Qn, preset, reset
  D_Flip_Flop d_ff_12 (.D(multiplexer_11_out), .clk(clk), .Q(out_4[11]));  // open: Qn, preset, reset
  D_Flip_Flop d_ff_13 (.D(multiplexer_12_out), .clk(clk), .Q(out_4[12]));  // open: Qn, preset, reset
  D_Flip_Flop d_ff_14 (.D(multiplexer_13_out), .clk(clk), .Q(out_4[13]));  // open: Qn, preset, reset
  D_Flip_Flop d_ff_15 (.D(multiplexer_14_out), .clk(clk), .Q(out_4[14]));  // open: Qn, preset, reset
  D_Flip_Flop d_ff_16 (.D(multiplexer_15_out), .clk(clk), .Q(out_4[15]));  // open: Qn, preset, reset
endmodule

module Reg12_LIC (
  input  [11:0] data,
  input  INR,
  input  clear,
  input  LD,
  input  clk,
  output [11:0] output_bits
);

  wire or_1_out;
  wire [11:0] adder_1_out, multiplexer_1_out, multiplexer_2_out;

  Multiplexer #(.width(12)) multiplexer_1 (.in0(data), .in1(adder_1_out), .out(multiplexer_1_out), .sel(INR));
  Multiplexer #(.width(12)) multiplexer_2 (
    .in0(multiplexer_1_out), .in1({12{1'b0}}), .out(multiplexer_2_out), .sel(clear));
  or or_1 (or_1_out, INR, clear, LD);
  Adder #(.width(12)) adder_1 (.a(12'h1), .b(output_bits), .out(adder_1_out));  // open: cin, cout
  Twelve_Bit_Register twelve_bit_register_1 (
    .input_bits(multiplexer_2_out), .clk(clk), .LD(or_1_out), .output_bits(output_bits));
endmodule

module Reg16_LIC (
  input  [15:0] data,
  input  INR,
  input  clear,
  input  LD,
  input  clk,
  output [15:0] output_bits
);

  wire or_1_out;
  wire [15:0] adder_1_out, multiplexer_1_out, multiplexer_2_out;

  Multiplexer #(.width(16)) multiplexer_1 (.in0(data), .in1(adder_1_out), .out(multiplexer_1_out), .sel(INR));
  Multiplexer #(.width(16)) multiplexer_2 (
    .in0(multiplexer_1_out), .in1({16{1'b0}}), .out(multiplexer_2_out), .sel(clear));
  or or_1 (or_1_out, INR, clear, LD);
  Adder #(.width(16)) adder_1 (.a(16'h1), .b(output_bits), .out(adder_1_out));  // open: cin, cout
  Sixteen_Bit_Register sixteen_bit_register_1 (
    .input_bits(multiplexer_2_out), .clk(clk), .enable(or_1_out), .out_4(output_bits));
endmodule

module AR (
  input  [11:0] D,
  input  INR,
  input  clear,
  input  LD,
  input  clk,
  output [11:0] output_bits
);

  Reg12_LIC reg12_lic_1 (.data(D), .INR(INR), .clear(clear), .LD(LD), .clk(clk), .output_bits(output_bits));
endmodule

module PC (
  input  [11:0] D,
  input  INR,
  input  clear,
  input  LD,
  input  clk,
  output [11:0] output_bits
);

  Reg12_LIC reg12_lic_1 (.data(D), .INR(INR), .clear(clear), .LD(LD), .clk(clk), .output_bits(output_bits));
endmodule

module DR (
  input  [15:0] D,
  input  INR,
  input  LD,
  input  clk,
  output [15:0] output_bits
);

  Reg16_LIC reg16_lic_1 (.data(D), .INR(INR), .clear(1'b0), .LD(LD), .clk(clk), .output_bits(output_bits));
endmodule

module AC (
  input  [15:0] D,
  input  INR,
  input  clear,
  input  LD,
  input  clk,
  output [15:0] output_bits
);

  Reg16_LIC reg16_lic_1 (.data(D), .INR(INR), .clear(clear), .LD(LD), .clk(clk), .output_bits(output_bits));
endmodule

module IR (
  input  [15:0] D,
  input  LD,
  input  clk,
  output [15:0] output_bits
);

  Sixteen_Bit_Register sixteen_bit_register_1 (.input_bits(D), .clk(clk), .enable(LD), .out_4(output_bits));
endmodule

module TR (
  input  [15:0] D,
  input  LD,
  input  clk,
  output [15:0] output_bits
);

  Sixteen_Bit_Register sixteen_bit_register_1 (.input_bits(D), .clk(clk), .enable(LD), .out_4(output_bits));
endmodule

module SC (
  input  INR,
  input  clear,
  input  clk,
  output [3:0] output_bits
);

  wire and_1_out, and_2_out, and_3_out, multiplexer_1_out, multiplexer_2_out, multiplexer_3_out,
       multiplexer_4_out;

  Multiplexer multiplexer_1 (.in0(INR), .in1(output_bits[0]), .out(multiplexer_1_out), .sel(clear));
  T_Flip_Flop t_ff_1 (.T(multiplexer_1_out), .clk(clk), .Q(output_bits[0]));  // open: Qn, reset, preset
  and and_1 (and_1_out, INR, output_bits[0]);
  Multiplexer multiplexer_2 (.in0(and_1_out), .in1(output_bits[1]), .out(multiplexer_2_out), .sel(clear));
  T_Flip_Flop t_ff_2 (.T(multiplexer_2_out), .clk(clk), .Q(output_bits[1]));  // open: Qn, reset, preset
  and and_2 (and_2_out, and_1_out, output_bits[1]);
  Multiplexer multiplexer_3 (.in0(and_2_out), .in1(output_bits[2]), .out(multiplexer_3_out), .sel(clear));
  T_Flip_Flop t_ff_3 (.T(multiplexer_3_out), .clk(clk), .Q(output_bits[2]));  // open: Qn, reset, preset
  and and_3 (and_3_out, and_2_out, output_bits[2]);
  Multiplexer multiplexer_4 (.in0(and_3_out), .in1(output_bits[3]), .out(multiplexer_4_out), .sel(clear));
  T_Flip_Flop t_ff_4 (.T(multiplexer_4_out), .clk(clk), .Q(output_bits[3]));  // open: Qn, reset, preset
endmodule

module Common_Bus (
  input  [11:0] SP,
  input  [11:0] AR,
  input  [11:0] PC,
  input  [15:0] DR,
  input  [15:0] AC,
  input  [15:0] IR,
  input  [15:0] TR,
  input  [15:0] MEM,
  input  [2:0] Sel,
  output [15:0] My_Bus
);

  wire [7:0] threebyeight_decoder_1_output_bits;
  wire [15:0] and_1_out, and_2_out, and_3_out, and_4_out, and_5_out, and_6_out, and_7_out, and_8_out,
       bit_extender_1_out, bit_extender_2_out, bit_extender_3_out, bit_extender_4_out, bit_extender_5_out,
       bit_extender_6_out, bit_extender_7_out, bit_extender_8_out, bit_extender_9_out, bit_extender_10_out,
       bit_extender_11_out;

  ThreebyEight_Decoder threebyeight_decoder_1 (
    .select_bits(Sel), .enable(1'b1), .output_bits(threebyeight_decoder_1_output_bits));
  assign bit_extender_1_out = {{4{1'b0}}, SP};  // Bit_Extender bit_extender_1
  assign bit_extender_2_out = {{15{threebyeight_decoder_1_output_bits[0]}}, threebyeight_decoder_1_output_bits[0]};  // Bit_Extender bit_extender_2
  assign bit_extender_3_out = {{15{threebyeight_decoder_1_output_bits[6]}}, threebyeight_decoder_1_output_bits[6]};  // Bit_Extender bit_extender_3
  assign bit_extender_4_out = {{15{threebyeight_decoder_1_output_bits[5]}}, threebyeight_decoder_1_output_bits[5]};  // Bit_Extender bit_extender_4
  assign bit_extender_5_out = {{15{threebyeight_decoder_1_output_bits[7]}}, threebyeight_decoder_1_output_bits[7]};  // Bit_Extender bit_extender_5
  assign bit_extender_6_out = {{4{1'b0}}, AR};  // Bit_Extender bit_extender_6
  assign bit_extender_7_out = {{15{threebyeight_decoder_1_output_bits[1]}}, threebyeight_decoder_1_output_bits[1]};  // Bit_Extender bit_extender_7
  assign bit_extender_8_out = {{4{1'b0}}, PC};  // Bit_Extender bit_extender_8
  assign bit_extender_9_out = {{15{threebyeight_decoder_1_output_bits[2]}}, threebyeight_decoder_1_output_bits[2]};  // Bit_Extender bit_extender_9
  assign bit_extender_10_out = {{15{threebyeight_decoder_1_output_bits[3]}}, threebyeight_decoder_1_output_bits[3]};  // Bit_Extender bit_extender_10
  assign bit_extender_11_out = {{15{threebyeight_decoder_1_output_bits[4]}}, threebyeight_decoder_1_output_bits[4]};  // Bit_Extender bit_extender_11
  assign and_1_out = TR & bit_extender_3_out;  // AND_Gate and_1, 16 bits wide
  assign and_2_out = bit_extender_1_out & bit_extender_2_out;  // AND_Gate and_2, 16 bits wide
  assign and_3_out = IR & bit_extender_4_out;  // AND_Gate and_3, 16 bits wide
  assign and_4_out = MEM & bit_extender_5_out;  // AND_Gate and_4, 16 bits wide
  assign and_5_out = bit_extender_6_out & bit_extender_7_out;  // AND_Gate and_5, 16 bits wide
  assign and_6_out = bit_extender_8_out & bit_extender_9_out;  // AND_Gate and_6, 16 bits wide
  assign and_7_out = DR & bit_extender_10_out;  // AND_Gate and_7, 16 bits wide
  assign and_8_out = AC & bit_extender_11_out;  // AND_Gate and_8, 16 bits wide
  assign My_Bus = and_2_out | and_5_out | and_6_out | and_7_out | and_3_out | and_1_out | and_4_out | and_8_out;  // OR_Gate or_1, 16 bits wide
endmodule

module SP (
  input  INR,
  input  DCR,
  input  INIT,
  input  clk,
  output [11:0] SP_out
);

  wire or_1_out;
  wire [11:0] adder_1_out, adder_2_out, multiplexer_1_out, multiplexer_2_out;

  Multiplexer #(.width(12)) multiplexer_1 (.in0(adder_1_out), .in1(adder_2_out), .out(multiplexer_1_out), .sel(INR));
  Multiplexer #(.width(12)) multiplexer_2 (
    .in0(multiplexer_1_out), .in1({12{1'b1}}), .out(multiplexer_2_out), .sel(INIT));
  or or_1 (or_1_out, INIT, INR, DCR);
  Twelve_Bit_Register twelve_bit_register_1 (
    .input_bits(multiplexer_2_out), .clk(clk), .LD(or_1_out), .output_bits(SP_out));
  Adder #(.width(12)) adder_1 (.a({12{1'b1}}), .b(SP_out), .out(adder_1_out));  // open: cin, cout
  Adder #(.width(12)) adder_2 (.a(12'h1), .b(SP_out), .out(adder_2_out));  // open: cin, cout
endmodule
